// Logisim project AR, PC.circ as structural Verilog
module AR (
  input  [7:0] in_1,
  input  [7:0] in_2,
  input  in_3,
  input  in_4
);

  wire clock_1_out;
  wire [4:0] bit_extender_1_out, d_ff_5_q;

  Bit_Extender #(.out_width(5)) bit_extender_1 (.in(in_2), .out(bit_extender_1_out));
  D_Flip_Flop d_ff_1 (
    .clk(clock_1_out), .D(bit_extender_1_out[4]), .Q(d_ff_5_q[4]), .en(in_4), .reset(in_3));  // open: Qn, preset
  D_Flip_Flop d_ff_2 (
    .clk(clock_1_out), .D(bit_extender_1_out[3]), .Q(d_ff_5_q[3]), .en(in_4), .reset(in_3));  // open: Qn, preset
  D_Flip_Flop d_ff_3 (
    .clk(clock_1_out), .D(bit_extender_1_out[2]), .Q(d_ff_5_q[2]), .en(in_4), .reset(in_3));  // open: Qn, preset
  D_Flip_Flop d_ff_4 (
    .clk(clock_1_out), .D(bit_extender_1_out[1]), .Q(d_ff_5_q[1]), .en(in_4), .reset(in_3));  // open: Qn, preset
  D_Flip_Flop d_ff_5 (
    .clk(clock_1_out), .D(bit_extender_1_out[0]), .Q(d_ff_5_q[0]), .en(in_4), .reset(in_3));  // open: Qn, preset
  Clock clock_1 (.out(clock_1_out));
  assign in_1 = {{3{1'b0}}, d_ff_5_q};  // Bit_Extender bit_extender_2
  // Probe on in_1
endmodule

module PC (
  input  in_1,
  input  [7:0] in_2,
  input  [7:0] in_3,
  input  in_4,
  input  in_5
);

  wire clock_1_out;
  wire [4:0] bit_extender_1_out, counter_1_q;

  // Probe on bit_extender_1_out
  Bit_Extender #(.out_width(5)) bit_extender_1 (.in(in_2), .out(bit_extender_1_out));
  Counter #(.width(5), .max('h1f)) counter_1 (
    .load(in_1), .D(bit_extender_1_out), .count(in_5), .Q(counter_1_q), .clk(clock_1_out), .clr(in_4));  // open: carry
  Clock clock_1 (.out(clock_1_out));
  assign in_3 = {{3{1'b0}}, counter_1_q};  // Bit_Extender bit_extender_2
  // Probe on in_3
endmodule
