// Logisim project Team Report (FINAL).circ as structural Verilog: 11 circuits, main circuit main
module main (
  output E
);

  wire clock_1_out, decode_1_ac_load, decode_1_ar_load, decode_1_dr_load, decode_1_ir_load,
       decode_1_memory_load, decode_1_pc_increment, decode_1_pc_load, decode_1_sc_clear, Reset, Start_out,
       timing_and_control_1_t0, timing_and_control_1_t1, timing_and_control_1_t2, timing_and_control_1_t3,
       timing_and_control_1_t4;
  wire [2:0] decode_1_select_bus, ir_1_opecode;
  wire [3:0] ac_1_out, ar_1_to_bus, bus_1_bus_out, dr_1_out, ir_1_out, pc_1_output, ram_1_data;
  wire [4:0] ar_1_to_memory;
  wire [7:0] add_logic_1_out;
  wire [7:4] ac_1_out_2, ar_1_to_bus_2, bus_1_bus_out_2, dr_1_out_2, ir_1_out_2, pc_1_output_2, ram_1_data_2;

  Button u_Reset (.out(Reset));
  Button Start (.out(Start_out));
  Timing_and_Control timing_and_control_1 (
    .T0(timing_and_control_1_t0), .T1(timing_and_control_1_t1), .T2(timing_and_control_1_t2),
    .T3(timing_and_control_1_t3), .T4(timing_and_control_1_t4), .Start(Start_out), .Reset(Reset),
    .Clear(decode_1_sc_clear));
  // Probe on ir_1_opecode
  Decode decode_1 (
    .T0(timing_and_control_1_t0), .T1(timing_and_control_1_t1), .T2(timing_and_control_1_t2),
    .T3(timing_and_control_1_t3), .T4(timing_and_control_1_t4), .PC_Load(decode_1_pc_load),
    .PC_Increment(decode_1_pc_increment), .AR_Load(decode_1_ar_load), .DR_Load(decode_1_dr_load),
    .AC_Load(decode_1_ac_load), .IR_Load(decode_1_ir_load), .Memory_Load(decode_1_memory_load),
    .Select_Bus(decode_1_select_bus), .SC_clear(decode_1_sc_clear), .Op(ir_1_opecode));
  Add_Logic add_logic_1 (
    .DR({dr_1_out_2, dr_1_out}), .AC({ac_1_out_2, ac_1_out}), .Out(add_logic_1_out), .Op(ir_1_opecode),
    .Cout(E));
  Clock clock_1 (.out(clock_1_out));
  RAM #(.addrWidth(5), .bus("separate")) ram_1 (
    .addr(ar_1_to_memory), .din({bus_1_bus_out_2, bus_1_bus_out}), .data({ram_1_data_2, ram_1_data}),
    .str(decode_1_memory_load), .clk(clock_1_out));  // open: sel, ld, clr
  AR ar_1 (
    .From_Bus({bus_1_bus_out_2, bus_1_bus_out}), .To_Bus({ar_1_to_bus_2, ar_1_to_bus}),
    .Load(decode_1_ar_load), .Clear(Reset), .To_Memory(ar_1_to_memory));
  PC pc_1 (
    .From_Bus({bus_1_bus_out_2, bus_1_bus_out}), .Output({pc_1_output_2, pc_1_output}),
    .Load(decode_1_pc_load), .Increment(decode_1_pc_increment), .Clear(Reset));
  DR dr_1 (
    .From_Bus({bus_1_bus_out_2, bus_1_bus_out}), .Out({dr_1_out_2, dr_1_out}), .Load(decode_1_dr_load),
    .Clear(Reset));
  AC ac_1 (.From_Bus(add_logic_1_out), .Out({ac_1_out_2, ac_1_out}), .Load(decode_1_ac_load), .Clear(Reset));
  IR ir_1 (
    .From_Bus({bus_1_bus_out_2, bus_1_bus_out}), .Out({ir_1_out_2, ir_1_out}), .Opecode(ir_1_opecode),
    .Load(decode_1_ir_load), .Clear(Reset));
  // Probe on {bus_1_bus_out_2, bus_1_bus_out}
  // Probe on decode_1_select_bus
  Hex_Digit_Display hex_digit_display_1 (.value(ram_1_data));  // open: dp
  Hex_Digit_Display hex_digit_display_2 (.value(ram_1_data_2));  // open: dp
  Hex_Digit_Display hex_digit_display_3 (.value(ar_1_to_bus_2));  // open: dp
  Hex_Digit_Display hex_digit_display_4 (.value(ar_1_to_bus));  // open: dp
  Hex_Digit_Display hex_digit_display_5 (.value(pc_1_output_2));  // open: dp
  Hex_Digit_Display hex_digit_display_6 (.value(pc_1_output));  // open: dp
  Hex_Digit_Display hex_digit_display_7 (.value(dr_1_out_2));  // open: dp
  Hex_Digit_Display hex_digit_display_8 (.value(dr_1_out));  // open: dp
  Hex_Digit_Display hex_digit_display_9 (.value(ac_1_out_2));  // open: dp
  Hex_Digit_Display hex_digit_display_10 (.value(ac_1_out));  // open: dp
  Hex_Digit_Display hex_digit_display_11 (.value(ir_1_out_2));  // open: dp
  Hex_Digit_Display hex_digit_display_12 (.value(ir_1_out));  // open: dp
  Hex_Digit_Display hex_digit_display_13 (.value(bus_1_bus_out_2));  // open: dp
  Hex_Digit_Display hex_digit_display_14 (.value(bus_1_bus_out));  // open: dp
  BUS bus_1 (
    .Select_Bus(decode_1_select_bus), .Memory({ram_1_data_2, ram_1_data}),
    .Adress_Register({ar_1_to_bus_2, ar_1_to_bus}), .Program_Counter({pc_1_output_2, pc_1_output}),
    .Data_Register({dr_1_out_2, dr_1_out}), .Accumulator({ac_1_out_2, ac_1_out}),
    .Instruction_Register({ir_1_out_2, ir_1_out}), .Bus_out({bus_1_bus_out_2, bus_1_bus_out}));
endmodule

module Timing_and_Control (
  input  Start,
  input  Reset,
  input  Clear,
  output T0,
  output T1,
  output T2,
  output T3,
  output T4
);

  wire and_1_out, clock_1_out, d_ff_1_q, d_ff_2_q, or_1_out;
  wire [2:0] Counter_q;

  Clock clock_1 (.out(clock_1_out));
  D_Flip_Flop d_ff_1 (.clk(Start), .D(1'b1), .Q(d_ff_1_q), .reset(Reset));  // open: Qn, preset, en
  Counter #(.width(3), .max('h7)) Counter (
    .count(and_1_out), .Q(Counter_q), .clk(and_1_out), .clr(or_1_out));  // open: load, D, carry
  and and_1 (and_1_out, clock_1_out, d_ff_1_q);
  or or_1 (or_1_out, Reset, d_ff_2_q);
  D_Flip_Flop d_ff_2 (.clk(clock_1_out), .D(Clear), .Q(d_ff_2_q), .reset(or_1_out));  // open: Qn, preset, en
  Decoder #(.select(3), .enable("false")) decoder_1 (
    .out0(T0), .out1(T1), .out2(T2), .out3(T3), .out4(T4), .sel(Counter_q));  // open: out5, out6, out7
endmodule

module Decode (
  input  T0,
  input  T1,
  input  T2,
  input  T3,
  input  T4,
  input  [2:0] Op,
  output Memory_Load,
  output AR_Load,
  output PC_Load,
  output PC_Increment,
  output DR_Load,
  output AC_Load,
  output IR_Load,
  output [2:0] Select_Bus,
  output SC_clear
);

  wire and_1_out, and_2_out, decoder_1_out0, decoder_1_out1, decoder_1_out2, decoder_1_out3, decoder_1_out4,
       or_1_out, or_2_out;

  Decoder #(.select(3), .enable("false")) decoder_1 (
    .out0(decoder_1_out0), .out1(decoder_1_out1), .out2(decoder_1_out2), .out3(decoder_1_out3),
    .out4(decoder_1_out4), .sel(Op));  // open: out5, out6, out7
  or or_1 (or_1_out, decoder_1_out2, decoder_1_out1, decoder_1_out0);
  and and_1 (and_1_out, T4, decoder_1_out2);
  or or_2 (or_2_out, decoder_1_out3, decoder_1_out4);
  and and_2 (and_2_out, T3, or_2_out);
  and and_3 (Memory_Load, decoder_1_out3, T3);
  or or_3 (AR_Load, T0, T2);
  and and_4 (PC_Load, T3, decoder_1_out4);
  and and_5 (DR_Load, T3, or_1_out);
  and and_6 (AC_Load, or_1_out, T4);
  or or_4 (Select_Bus[0], and_1_out, PC_Load, DR_Load, T1, T2);
  or or_5 (Select_Bus[1], DR_Load, T1, and_1_out, T0);
  or or_6 (Select_Bus[2], DR_Load, T1, Memory_Load, T2);
  or or_7 (SC_clear, AC_Load, and_2_out);

  assign IR_Load = T1;
  assign PC_Increment = T1;

  // Notes on the sheet:
  //   D0
  //   D1
  //   D2
  //   D3
  //   D4
endmodule

module BUS (
  input  [2:0] Select_Bus,
  input  [7:0] Memory,
  input  [7:0] Adress_Register,
  input  [7:0] Program_Counter,
  input  [7:0] Data_Register,
  input  [7:0] Accumulator,
  input  [7:0] Instruction_Register,
  output [7:0] Bus_out
);

  Multiplexer #(.select(3), .width(8), .enable("false")) multiplexer_1 (
    .in1(Adress_Register), .in2(Program_Counter), .in3(Data_Register), .in4(Accumulator),
    .in5(Instruction_Register), .in7(Memory), .out(Bus_out), .sel(Select_Bus));  // open: in0, in6
endmodule

module AR (
  input  [7:0] From_Bus,
  input  Load,
  input  Clear,
  output [4:0] To_Memory,
  output [7:0] To_Bus
);

  wire clock_1_out;
  wire [4:0] bit_extender_1_out;

  Bit_Extender #(.out_width(5)) bit_extender_1 (.in(From_Bus), .out(bit_extender_1_out));
  D_Flip_Flop _0 (
    .clk(clock_1_out), .D(bit_extender_1_out[4]), .Q(To_Memory[4]), .en(Load), .reset(Clear));  // open: Qn, preset
  D_Flip_Flop _1 (
    .clk(clock_1_out), .D(bit_extender_1_out[3]), .Q(To_Memory[3]), .en(Load), .reset(Clear));  // open: Qn, preset
  D_Flip_Flop _2 (
    .clk(clock_1_out), .D(bit_extender_1_out[2]), .Q(To_Memory[2]), .en(Load), .reset(Clear));  // open: Qn, preset
  D_Flip_Flop _3 (
    .clk(clock_1_out), .D(bit_extender_1_out[1]), .Q(To_Memory[1]), .en(Load), .reset(Clear));  // open: Qn, preset
  D_Flip_Flop _4 (
    .clk(clock_1_out), .D(bit_extender_1_out[0]), .Q(To_Memory[0]), .en(Load), .reset(Clear));  // open: Qn, preset
  Clock clock_1 (.out(clock_1_out));
  assign To_Bus = {{3{1'b0}}, To_Memory};  // Bit_Extender bit_extender_2
endmodule

module PC (
  input  Load,
  input  [7:0] From_Bus,
  input  Increment,
  input  Clear,
  output [7:0] Output
);

  wire clock_1_out;
  wire [4:0] bit_extender_1_out, counter_1_q;

  Bit_Extender #(.out_width(5)) bit_extender_1 (.in(From_Bus), .out(bit_extender_1_out));
  Counter #(.width(5), .max('h1f)) counter_1 (
    .load(Load), .D(bit_extender_1_out), .count(Increment), .Q(counter_1_q), .clk(clock_1_out), .clr(Clear));  // open: carry
  Clock clock_1 (.out(clock_1_out));
  assign Output = {{3{1'b0}}, counter_1_q};  // Bit_Extender bit_extender_2
endmodule

module Add_Logic (
  input  [7:0] DR,
  input  [2:0] Op,
  input  [7:0] AC,
  output [7:0] Out,
  output Cout
);

  wire and_1_out, and_2_out, clock_1_out, n1_bit_logic_circuit_1_cout, n1_bit_logic_circuit_2_cout,
       n1_bit_logic_circuit_3_cout, n1_bit_logic_circuit_4_cout, n1_bit_logic_circuit_5_cout,
       n1_bit_logic_circuit_6_cout, n1_bit_logic_circuit_7_cout, n1_bit_logic_circuit_8_cout, not_1_out,
       not_2_out;

  _1_bit_Logic_Circuit u_1_bit_logic_circuit_1 (
    .DR(DR[0]), .AC(AC[0]), .Out(Out[0]), .Cout(n1_bit_logic_circuit_1_cout), .Op(Op), .Cin(1'b0));
  _1_bit_Logic_Circuit u_1_bit_logic_circuit_2 (
    .DR(DR[1]), .AC(AC[1]), .Out(Out[1]), .Cout(n1_bit_logic_circuit_2_cout), .Op(Op),
    .Cin(n1_bit_logic_circuit_1_cout));
  _1_bit_Logic_Circuit u_1_bit_logic_circuit_3 (
    .DR(DR[2]), .AC(AC[2]), .Out(Out[2]), .Cout(n1_bit_logic_circuit_3_cout), .Op(Op),
    .Cin(n1_bit_logic_circuit_2_cout));
  _1_bit_Logic_Circuit u_1_bit_logic_circuit_4 (
    .DR(DR[3]), .AC(AC[3]), .Out(Out[3]), .Cout(n1_bit_logic_circuit_4_cout), .Op(Op),
    .Cin(n1_bit_logic_circuit_3_cout));
  _1_bit_Logic_Circuit u_1_bit_logic_circuit_5 (
    .DR(DR[4]), .AC(AC[4]), .Out(Out[4]), .Cout(n1_bit_logic_circuit_5_cout), .Op(Op),
    .Cin(n1_bit_logic_circuit_4_cout));
  _1_bit_Logic_Circuit u_1_bit_logic_circuit_6 (
    .DR(DR[5]), .AC(AC[5]), .Out(Out[5]), .Cout(n1_bit_logic_circuit_6_cout), .Op(Op),
    .Cin(n1_bit_logic_circuit_5_cout));
  _1_bit_Logic_Circuit u_1_bit_logic_circuit_7 (
    .DR(DR[6]), .AC(AC[6]), .Out(Out[6]), .Cout(n1_bit_logic_circuit_7_cout), .Op(Op),
    .Cin(n1_bit_logic_circuit_6_cout));
  _1_bit_Logic_Circuit u_1_bit_logic_circuit_8 (
    .DR(DR[7]), .AC(AC[7]), .Out(Out[7]), .Cout(n1_bit_logic_circuit_8_cout), .Op(Op),
    .Cin(n1_bit_logic_circuit_7_cout));
  not not_1 (not_1_out, Op[1]);
  not not_2 (not_2_out, Op[2]);
  Clock clock_1 (.out(clock_1_out));
  and and_1 (and_1_out, not_2_out, not_1_out, Op[0]);
  and and_2 (and_2_out, and_1_out, clock_1_out);
  D_Flip_Flop d_ff_1 (.clk(and_2_out), .D(n1_bit_logic_circuit_8_cout), .Q(Cout));  // open: Qn, preset, en, reset
endmodule

module AC (
  input  [7:0] From_Bus,
  input  Clear,
  input  Load,
  output [7:0] Out
);

  wire clock_1_out;

  Clock clock_1 (.out(clock_1_out));
  D_Flip_Flop _0 (.clk(clock_1_out), .D(From_Bus[0]), .Q(Out[0]), .en(Load), .reset(Clear));  // open: Qn, preset
  D_Flip_Flop _1 (.clk(clock_1_out), .D(From_Bus[1]), .Q(Out[1]), .en(Load), .reset(Clear));  // open: Qn, preset
  D_Flip_Flop _2 (.clk(clock_1_out), .D(From_Bus[2]), .Q(Out[2]), .en(Load), .reset(Clear));  // open: Qn, preset
  D_Flip_Flop _3 (.clk(clock_1_out), .D(From_Bus[3]), .Q(Out[3]), .en(Load), .reset(Clear));  // open: Qn, preset
  D_Flip_Flop _4 (.clk(clock_1_out), .D(From_Bus[4]), .Q(Out[4]), .en(Load), .reset(Clear));  // open: Qn, preset
  D_Flip_Flop _5 (.clk(clock_1_out), .D(From_Bus[5]), .Q(Out[5]), .en(Load), .reset(Clear));  // open: Qn, preset
  D_Flip_Flop _6 (.clk(clock_1_out), .D(From_Bus[6]), .Q(Out[6]), .en(Load), .reset(Clear));  // open: Qn, preset
  D_Flip_Flop _7 (.clk(clock_1_out), .D(From_Bus[7]), .Q(Out[7]), .en(Load), .reset(Clear));  // open: Qn, preset
endmodule

module IR (
  input  [7:0] From_Bus,
  input  Clear,
  input  Load,
  output [7:0] Out,
  output [2:0] Opecode
);

  wire clock_1_out;

  Clock clock_1 (.out(clock_1_out));
  D_Flip_Flop _0 (.clk(clock_1_out), .D(From_Bus[0]), .Q(Out[0]), .en(Load), .reset(Clear));  // open: Qn, preset
  D_Flip_Flop _1 (.clk(clock_1_out), .D(From_Bus[1]), .Q(Out[1]), .en(Load), .reset(Clear));  // open: Qn, preset
  D_Flip_Flop _2 (.clk(clock_1_out), .D(From_Bus[2]), .Q(Out[2]), .en(Load), .reset(Clear));  // open: Qn, preset
  D_Flip_Flop _3 (.clk(clock_1_out), .D(From_Bus[3]), .Q(Out[3]), .en(Load), .reset(Clear));  // open: Qn, preset
  D_Flip_Flop _4 (.clk(clock_1_out), .D(From_Bus[4]), .Q(Out[4]), .en(Load), .reset(Clear));  // open: Qn, preset
  D_Flip_Flop _5 (.clk(clock_1_out), .D(From_Bus[5]), .Q(Opecode[0]), .en(Load), .reset(Clear));  // open: Qn, preset
  D_Flip_Flop _6 (.clk(clock_1_out), .D(From_Bus[6]), .Q(Opecode[1]), .en(Load), .reset(Clear));  // open: Qn, preset
  D_Flip_Flop _7 (.clk(clock_1_out), .D(From_Bus[7]), .Q(Opecode[2]), .en(Load), .reset(Clear));  // open: Qn, preset

  assign Out[7:5] = Opecode;
endmodule

module DR (
  input  [7:0] From_Bus,
  input  Clear,
  input  Load,
  output [7:0] Out
);

  wire clock_1_out;

  Clock clock_1 (.out(clock_1_out));
  D_Flip_Flop _0 (.clk(clock_1_out), .D(From_Bus[0]), .Q(Out[0]), .en(Load), .reset(Clear));  // open: Qn, preset
  D_Flip_Flop _1 (.clk(clock_1_out), .D(From_Bus[1]), .Q(Out[1]), .en(Load), .reset(Clear));  // open: Qn, preset
  D_Flip_Flop _2 (.clk(clock_1_out), .D(From_Bus[2]), .Q(Out[2]), .en(Load), .reset(Clear));  // open: Qn, preset
  D_Flip_Flop _3 (.clk(clock_1_out), .D(From_Bus[3]), .Q(Out[3]), .en(Load), .reset(Clear));  // open: Qn, preset
  D_Flip_Flop _4 (.clk(clock_1_out), .D(From_Bus[4]), .Q(Out[4]), .en(Load), .reset(Clear));  // open: Qn, preset
  D_Flip_Flop _5 (.clk(clock_1_out), .D(From_Bus[5]), .Q(Out[5]), .en(Load), .reset(Clear));  // open: Qn, preset
  D_Flip_Flop _6 (.clk(clock_1_out), .D(From_Bus[6]), .Q(Out[6]), .en(Load), .reset(Clear));  // open: Qn, preset
  D_Flip_Flop _7 (.clk(clock_1_out), .D(From_Bus[7]), .Q(Out[7]), .en(Load), .reset(Clear));  // open: Qn, preset
endmodule

module _1_bit_Logic_Circuit (
  input  Cin,
  input  DR,
  input  AC,
  input  [2:0] Op,
  output Out,
  output Cout
);

  wire adder_1_cout, adder_1_out, and_2_out, and_3_out, not_1_out, not_2_out;

  Adder #(.width(1)) adder_1 (.a(DR), .b(AC), .out(adder_1_out), .cin(Cin), .cout(adder_1_cout));
  and and_1 (Cout, adder_1_cout, and_3_out);
  and and_2 (and_2_out, DR, AC);
  not not_1 (not_1_out, Op[1]);
  not not_2 (not_2_out, Op[2]);
  and and_3 (and_3_out, Op[0], not_1_out, not_2_out);
  Multiplexer #(.select(3), .enable("false")) multiplexer_1 (
    .in0(and_2_out), .in1(adder_1_out), .in2(DR), .out(Out), .sel(Op));  // open: in3, in4, in5, in6, in7
endmodule
