// Logisim project Computer Architecture Logisim1_1.circ as structural Verilog: 1 circuit, main circuit main
module main (
  input  Serial_Input,
  input  I0,
  input  I1,
  input  I2,
  input  Serial_Input_2,
  input  I3,
  input  Enable,
  input  S0,
  input  S1
);

  wire clock_1_out, d_ff_1_q, d_ff_2_q, d_ff_3_q, d_ff_4_q, multiplexer_1_out, multiplexer_2_out,
       multiplexer_3_out, multiplexer_4_out, undriven, undriven_2, undriven_3, undriven_4;

  Multiplexer #(.select(2)) multiplexer_1 (
    .in0(d_ff_1_q), .in1(Serial_Input), .in2(d_ff_2_q), .in3(I0), .out(multiplexer_1_out), .sel({S1, S0}),
    .en(Enable));
  Multiplexer #(.select(2)) multiplexer_2 (
    .in0(d_ff_2_q), .in1(d_ff_1_q), .in2(d_ff_3_q), .in3(I1), .out(multiplexer_2_out), .sel({S1, S0}),
    .en(Enable));
  Multiplexer #(.select(2)) multiplexer_3 (
    .in0(d_ff_3_q), .in1(d_ff_2_q), .in2(d_ff_4_q), .in3(I2), .out(multiplexer_3_out), .sel({S1, S0}),
    .en(Enable));
  Multiplexer #(.select(2)) multiplexer_4 (
    .in0(d_ff_4_q), .in1(d_ff_3_q), .in2(Serial_Input_2), .in3(I3), .out(multiplexer_4_out), .sel({S1, S0}),
    .en(Enable));
  Clock clock_1 (.out(clock_1_out));
  // Probe on d_ff_1_q
  D_Flip_Flop d_ff_1 (
    .clk(clock_1_out), .D(multiplexer_1_out), .Q(d_ff_1_q), .en(undriven));  // open: Qn, preset, reset
  D_Flip_Flop d_ff_2 (
    .clk(clock_1_out), .D(multiplexer_2_out), .Q(d_ff_2_q), .en(undriven_2));  // open: Qn, preset, reset
  // Probe on d_ff_2_q
  // Probe on d_ff_3_q
  D_Flip_Flop d_ff_3 (
    .clk(clock_1_out), .D(multiplexer_3_out), .Q(d_ff_3_q), .en(undriven_3));  // open: Qn, preset, reset
  D_Flip_Flop d_ff_4 (
    .clk(clock_1_out), .D(multiplexer_4_out), .Q(d_ff_4_q), .en(undriven_4));  // open: Qn, preset, reset
  // Probe on d_ff_4_q
endmodule
