// Logisim project Computer Architecture Logisim1_2.circ as structural Verilog: 1 circuit, main circuit main
module main (
  input  Cin,
  input  S0,
  input  S1,
  input  A0,
  input  in_5,
  input  A1,
  input  in_7,
  input  A2,
  input  in_9,
  input  A3,
  input  in_11
);

  wire adder_1_cout, adder_1_out, adder_2_cout, adder_2_out, adder_3_cout, adder_3_out, adder_4_cout,
       adder_4_out, multiplexer_1_out, multiplexer_2_out, multiplexer_3_out, multiplexer_4_out, not_1_out,
       not_2_out, not_3_out, not_4_out, not_5_out;

  not not_1 (not_1_out, in_5);
  not not_2 (not_2_out, in_7);
  not not_3 (not_3_out, in_9);
  not not_4 (not_4_out, in_11);
  not not_5 (not_5_out, 1'b1);
  Multiplexer #(.select(2), .enable("false")) multiplexer_1 (
    .in0(in_5), .in1(not_1_out), .in2(not_5_out), .in3(1'b1), .out(multiplexer_1_out), .sel({S1, S0}));
  Multiplexer #(.select(2), .enable("false")) multiplexer_2 (
    .in0(in_7), .in1(not_2_out), .in2(not_5_out), .in3(1'b1), .out(multiplexer_2_out), .sel({S1, S0}));
  Multiplexer #(.select(2), .enable("false")) multiplexer_3 (
    .in0(in_9), .in1(not_3_out), .in2(not_5_out), .in3(1'b1), .out(multiplexer_3_out), .sel({S1, S0}));
  Multiplexer #(.select(2), .enable("false")) multiplexer_4 (
    .in0(in_11), .in1(not_4_out), .in2(not_5_out), .in3(1'b1), .out(multiplexer_4_out), .sel({S1, S0}));
  // Probe on adder_1_out
  Adder #(.width(1)) adder_1 (.a(A0), .b(multiplexer_1_out), .out(adder_1_out), .cin(Cin), .cout(adder_1_cout));
  // Probe on adder_2_out
  Adder #(.width(1)) adder_2 (
    .a(A1), .b(multiplexer_2_out), .out(adder_2_out), .cin(adder_1_cout), .cout(adder_2_cout));
  // Probe on adder_3_out
  Adder #(.width(1)) adder_3 (
    .a(A2), .b(multiplexer_3_out), .out(adder_3_out), .cin(adder_2_cout), .cout(adder_3_cout));
  Adder #(.width(1)) adder_4 (
    .a(A3), .b(multiplexer_4_out), .out(adder_4_out), .cin(adder_3_cout), .cout(adder_4_cout));
  // Probe on adder_4_out
  // Probe on adder_4_cout
endmodule
