// Logisim project Computer Architecture Logisim1_3_2.circ as structural Verilog: 1 circuit, main circuit main
module main (
  input  A0,
  input  A1,
  input  E
);

  wire nand_1_out, nand_2_out, nand_3_out, nand_4_out, not_1_out, not_2_out, not_3_out;

  not not_1 (not_1_out, A1);
  not not_2 (not_2_out, A0);
  not not_3 (not_3_out, E);
  // Probe on nand_1_out
  nand nand_1 (nand_1_out, not_2_out, not_1_out, not_3_out);
  nand nand_2 (nand_2_out, A0, not_1_out, not_3_out);
  // Probe on nand_2_out
  nand nand_3 (nand_3_out, not_2_out, A1, not_3_out);
  // Probe on nand_3_out
  // Probe on nand_4_out
  nand nand_4 (nand_4_out, A0, A1, not_3_out);
endmodule
