// Logisim project Computer Architecture Logisim_1_3_4.circ as structural Verilog: 1 circuit, main circuit main
module main (
  input  I0,
  input  I1,
  input  I2,
  input  I3,
  input  S0,
  input  S1
);

  wire and_1_out, and_2_out, and_3_out, and_4_out, not_1_out, not_2_out, or_1_out;

  and and_1 (and_1_out, I0, not_1_out, not_2_out);
  and and_2 (and_2_out, I1, S0, not_2_out);
  and and_3 (and_3_out, I2, not_1_out, S1);
  and and_4 (and_4_out, I3, S0, S1);
  not not_1 (not_1_out, S0);
  not not_2 (not_2_out, S1);
  // Probe on or_1_out
  or or_1 (or_1_out, and_1_out, and_2_out, and_3_out, and_4_out);
endmodule
